# Fritzing sketch Slave_V2 (saved by Fritzing 0.9.3b)
stripboards: 2

parts:
  U2 = Header 8 [package=1x08_smd]
  U3 = Header 8 [package=1x08_smd]
  S3 = Pushbutton [package="[THT]"]
  RS3 = Resistor [tolerance=±5% resistance=10k package="0603 [SMD]"]
  JP1 = Header 6 [package=1x06_smd_straight_alt]
  R2 = Resistor [tolerance=±5% resistance=220 package="0603 [SMD]"]
  JP3 = Header 6 [package=1x06_smd_straight_alt]
  J6-I2C = female pin header, 4 pins [form="♀ (female)"]
  J7-MIDI = female pin header, 3 pins [form="♀ (female)"]
  J10 = female pin header, 5 pins [form="♀ (female)"]
  J9 = male pin header, 20 pins [form="♂ (male)"]
  J8 = male pin header, 20 pins [form="♂ (male)"]
  JP4 = Header 6 [package=1x06_smd_straight_alt]
  JP5 = Header 6 [package=1x06_smd_straight_alt]
  I2C = female pin header, 4 pins [form="♀ (female)"]
  MIDI = female pin header, 3 pins [form="♀ (female)"]
  J13 = female pin header, 2 pins [form="♀ (female)"]
  R3 = Resistor [tolerance=±5% resistance=220 package="0603 [SMD]"]
  S5 = Pushbutton [package="[THT]"]
  SU = Pushbutton [package="[THT]"]
  S6 = Pushbutton [package="[THT]"]
  SL = Pushbutton [package="[THT]"]
  SD = Pushbutton [package="[THT]"]
  SR = Pushbutton [package="[THT]"]
  LEDR = LED - 5mm [color="Red (633nm)" package="5 mm [THT]"]
  LEDG = LED - 5mm [color="Green (565nm)" package="5 mm [THT]"]
  R5 = Resistor [tolerance=±5% resistance=33k package=THT]
  R6 = Resistor [tolerance=±5% resistance=33k package=THT]
  R-SL = Resistor [tolerance=±5% resistance=33k package=THT]
  RR = Resistor [tolerance=±5% resistance=33k package=THT]
  RD = Resistor [tolerance=±5% resistance=33k package=THT]
  RLG = Resistor [tolerance=±5% resistance=220 package=THT]
  RLR = Resistor [tolerance=±5% resistance=220 package=THT]
  RU = Resistor [tolerance=±5% resistance=33k package=THT]

nets:
  +5V: U2.1, JP1.1, JP3.1, J6-I2C.pin1, J10.pin5, J9.pin1, JP4.1, JP5.1, I2C.pin1, R3.Pin_0
  GND: U2.2, RS3.Pin_1, JP1.2, JP1.3, JP3.2, JP3.3, J6-I2C.pin2, J7-MIDI.pin2, J10.pin1, J9.pin3, JP4.2, JP4.3, JP5.2, JP5.3, I2C.pin2, MIDI.pin2, LEDR.cathode, LEDG.cathode, R5.Pin_1, R6.Pin_1, R-SL.Pin_1, RR.Pin_1, RD.Pin_1, RU.Pin_0
  N1: U2.3, JP1.4, JP4.4
  N2: U2.5, J9.pin4
  N3: U2.7, JP1.5, JP4.5
  WM-TX: U2.8, R2.Pin_0
  +3.3V: U3.1, S3.Pin_1, S3.Pin_2, J8.pin1, J13.pin2, S5.Pin_3, S5.Pin_4, SU.Pin_3, SU.Pin_4, S6.Pin_3, S6.Pin_4, SL.Pin_1, SL.Pin_2, SD.Pin_3, SD.Pin_4, SR.Pin_3, SR.Pin_4
  N4: U3.2, JP1.6, JP4.6
  N5: U3.3, S3.Pin_3, S3.Pin_4, RS3.Pin_0, J13.pin1
  WM-D5: U3.5, S5.Pin_1, S5.Pin_2, R5.Pin_0
  N6: R2.Pin_1, J7-MIDI.pin3, MIDI.pin3
  N7: JP3.4, J8.pin18, JP5.4
  N8: JP3.5, J9.pin20, JP5.5
  N9: JP3.6, J9.pin6, JP5.6
  RPI3-SDA: J6-I2C.pin3, J8.pin2, I2C.pin3
  RPI5-SDL: J6-I2C.pin4, J8.pin3, I2C.pin4
  N10: J7-MIDI.pin1, MIDI.pin1, R3.Pin_1
  RPI16-G23: J9.pin8, SR.Pin_1, SR.Pin_2, RR.Pin_0
  RPI18-GPIO24: J9.pin9, SU.Pin_1, SU.Pin_2, RU.Pin_1
  RPI11_G17: J8.pin6, S6.Pin_1, S6.Pin_2, R6.Pin_0
  RPI13_G27: J8.pin7, SL.Pin_3, SL.Pin_4, R-SL.Pin_0
  RPI15_G22: J8.pin8, SD.Pin_1, SD.Pin_2, RD.Pin_0
  N11: LEDR.anode, RLR.Pin_0
  N12: LEDG.anode, RLG.Pin_0

notes:
  Audio1
  Audio2
  I2C
  Ser
  MIDI
  Vert = 5, Jaune =2, Orange=4
  USB
