# Fritzing sketch Slave_V3 (saved by Fritzing 1.0.6)
stripboards: 2

parts:
  U2 = Header 8 [package=1x08_smd]
  U3 = Header 8 [package=1x08_smd]
  RS3 = Resistor [tolerance=±5% resistance=10k package="0603 [SMD]"]
  JP1-A2 = Header 6 [package=1x06_smd_straight_alt]
  R2 = Resistor [tolerance=±5% resistance=220 package="0603 [SMD]"]
  JP3-A1 = Header 6 [package=1x06_smd_straight_alt]
  J6-I2C = female pin header, 4 pins [form="♀ (female)"]
  J7-MIDI = female pin header, 3 pins [form="♀ (female)"]
  J10 = female pin header, 5 pins [form="♀ (female)"]
  AUDIO2 = Header 6 [package=1x06_smd_straight_alt]
  AUDIO1 = Header 6 [package=1x06_smd_straight_alt]
  I2C = female pin header, 4 pins [form="♀ (female)"]
  MIDI = female pin header, 3 pins [form="♀ (female)"]
  J13 = female pin header, 2 pins [form="♀ (female)"]
  R3 = Resistor [tolerance=±5% resistance=220 package="0603 [SMD]"]
  S5 = Pushbutton [package="[THT]"]
  SU = Pushbutton [package="[THT]"]
  S6 = Pushbutton [package="[THT]"]
  SL = Pushbutton [package="[THT]"]
  SD = Pushbutton [package="[THT]"]
  SR = Pushbutton [package="[THT]"]
  LEDR = LED - 5mm [color="Red (633nm)" current=0.030A package="5 mm [THT]"]
  R5 = Resistor [tolerance=±5% resistance=33k power=0.25W package=THT]
  R6 = Resistor [tolerance=±5% resistance=33k power=0.25W package=THT]
  R-SL = Resistor [tolerance=±5% resistance=33k power=0.25W package=THT]
  RR = Resistor [tolerance=±5% resistance=33k power=0.25W package=THT]
  RD = Resistor [tolerance=±5% resistance=33k power=0.25W package=THT]
  RLG = Resistor [tolerance=±5% resistance=220 power=0.25W package=THT]
  RLR = Resistor [tolerance=±5% resistance=220 power=0.25W package=THT]
  RU = Resistor [tolerance=±5% resistance=33k power=0.25W package=THT]
  JUSB = female pin header, 5 pins [form="♀ (female)"]
  SPow = Toggle Switch [package=THT]
  J8 = male pin header, 20 pins [form="♂ (male)"]
  J9 = male pin header, 20 pins [form="♂ (male)"]
  S3 = Pushbutton [package="[THT]"]

nets:
  +5V: U2.1, JP1-A2.1, JP3-A1.1, J6-I2C.pin1, J10.pin5, AUDIO2.1, AUDIO1.1, I2C.pin1, R3.Pin_0, SPow.L2, J9.pin1
  GND: U2.2, RS3.Pin_1, JP1-A2.2, JP1-A2.3, JP3-A1.2, JP3-A1.3, J6-I2C.pin2, J7-MIDI.pin2, J10.pin1, AUDIO2.2, AUDIO2.3, AUDIO1.2, AUDIO1.3, I2C.pin2, MIDI.pin2, LEDR.cathode, R5.Pin_1, R6.Pin_1, R-SL.Pin_1, RR.Pin_1, RD.Pin_1, RU.Pin_0, JUSB.pin1, J9.pin3
  WM-D4: U2.3, JP1-A2.4, AUDIO2.4
  WM-RX: U2.7, JP1-A2.5, AUDIO2.5
  WM-TX: U2.8, R2.Pin_0
  +3.3V: U3.1, J13.pin2, S5.Pin_3, S5.Pin_4, SU.Pin_3, SU.Pin_4, S6.Pin_3, S6.Pin_4, SL.Pin_1, SL.Pin_2, SD.Pin_3, SD.Pin_4, SR.Pin_3, SR.Pin_4, J8.pin1, S3.Pin_1, S3.Pin_2
  WM-D8: U3.2, JP1-A2.6, AUDIO2.6
  N1: U3.3, RS3.Pin_0, J13.pin1
  N2: R2.Pin_1, J7-MIDI.pin3, MIDI.pin3
  RPI35_G19: JP3-A1.4, AUDIO1.4, J8.pin18
  RPI40-G21: JP3-A1.5, AUDIO1.5, J9.pin20
  RPI12-G18: JP3-A1.6, AUDIO1.6, J9.pin6
  RPI3-SDA: J6-I2C.pin3, I2C.pin3, J8.pin2
  RPI5-SDL: J6-I2C.pin4, I2C.pin4, J8.pin3
  N3: J7-MIDI.pin1, MIDI.pin1, R3.Pin_1
  WM-D5: S5.Pin_1, S5.Pin_2, R5.Pin_0, J8.pin16
  RPI18-GPIO24: SU.Pin_1, SU.Pin_2, RU.Pin_1, J9.pin9
  RPI11_G17: S6.Pin_1, S6.Pin_2, R6.Pin_0, J8.pin6
  RPI13_G27: SL.Pin_3, SL.Pin_4, R-SL.Pin_0, J8.pin7
  RPI15_G22: SD.Pin_1, SD.Pin_2, RD.Pin_0, J8.pin8
  RPI16-G23: SR.Pin_1, SR.Pin_2, RR.Pin_0, J9.pin8
  N4: LEDR.anode, RLG.Pin_0
  WM-D6: RLG.Pin_1, J8.pin17
  RPI29-G5: RLR.Pin_1
  N5: JUSB.pin5, SPow.COM
  UART_: J9.pin4

notes:
  Audio1
  Unused
  I2C
  Ser (MIDI Tx)
  MIDI
  Pin4 => Jaune(5V)
  USB
  D6
  D5
  Pin5 =>orange(DATA)
