# Fritzing sketch slave (saved by Fritzing 0.9.3b)
stripboards: 1
perfboards: 1

parts:
  U2 = Header 8 [package=1x08_smd]
  U3 = Header 8 [package=1x08_smd]
  WeMos_D1_Mini1 = WeMos D1 Mini  # not connected
  S3 = Pushbutton [package="[THT]"]
  R1 = Resistor [tolerance=±5% resistance=10k package="0603 [SMD]"]
  JP1 = Header 6 [package=1x06_smd_straight_alt]
  R2 = Resistor [tolerance=±5% resistance=220 package="0603 [SMD]"]
  U4 = MIDI_CONN_FEMALE [package=din_5_female]
  R3 = Resistor [tolerance=±5% resistance=220 package="0603 [SMD]"]
  J1 = shrouded pin header, 40 pins [form="♂ (shrouded male)"]
  JP3 = Header 6 [package=1x06_smd_straight_alt]
  J2 = female pin header, 2 pins [form="♀ (female)"]
  J3 = female pin header, 2 pins [form="♀ (female)"]
  J4 = male pin header, 4 pins [form="♂ (male)"]

nets:
  N1: U2.1, S3.Pin_3, S3.Pin_4, JP1.1, R3.Pin_1, J1.pin40, JP3.6, J2.pin1
  N2: U2.2, R1.Pin_0, JP1.2, JP1.3, U4.NC2, J1.pin38, JP3.5
  N3: U2.3, JP1.4
  N4: U2.5, J1.pin37, J4.pin4
  N5: U2.7, JP1.5
  N6: U2.8, R2.Pin_0
  N7: U3.2, JP1.6
  N8: U3.3, S3.Pin_1, S3.Pin_2, R1.Pin_1
  N9: R2.Pin_1, U4.MIDI_OUT
  N10: U4.MIDI_IN, R3.Pin_0
  N11: J1.pin2, J3.pin2
  N12: J1.pin3, J3.pin1
  N13: J1.pin18, JP3.3
  N14: J1.pin21, JP3.2
  N15: J1.pin35, JP3.1

notes:
  Audio1
  Audio2
  I2C
  Ser
